// Digital circuit ALU.dig as structural Verilog
module ALU (
  input  [31:0] A,
  input  [31:0] B,
  input  [4:0] Op,
  input  Mode,
  input  [31:0] Immediate,
  output [31:0] O
);

  wire [5:0] multiplexer_1_out;
  wire [31:0] add_1_s, and_1_out, barrelshifter_1_out, barrelshifter_2_out, barrelshifter_3_out,
       barrelshifter_4_out, barrelshifter_5_out, barrelshifter_6_out, nand_1_out, neg_1_out, or_1_out,
       sub_1_s, xor_1_out;
  wire [31:6] multiplexer_1_out_2;

  Multiplexer #(.Bits(32)) multiplexer_1 (
    .sel(Mode), .in_0(B), .in_1(Immediate), .out({multiplexer_1_out_2, multiplexer_1_out}));
  Multiplexer #(.Selector_Bits(5), .Bits(32)) multiplexer_2 (
    .sel(Op), .in_0({multiplexer_1_out_2, multiplexer_1_out}), .in_1(barrelshifter_1_out), .in_2(add_1_s),
    .in_3(sub_1_s), .in_4(neg_1_out), .in_5(and_1_out), .in_6(or_1_out), .in_7(nand_1_out), .in_8(xor_1_out),
    .in_9(barrelshifter_2_out), .in_10(barrelshifter_3_out), .in_11(barrelshifter_4_out),
    .in_12(barrelshifter_5_out), .in_13(barrelshifter_6_out), .in_14({32{1'b0}}), .in_15({32{1'b0}}),
    .in_16({32{1'b0}}), .in_17({32{1'b0}}), .in_18({32{1'b0}}), .in_19({32{1'b0}}), .in_20({32{1'b0}}),
    .in_21({32{1'b0}}), .in_22({32{1'b0}}), .in_23({32{1'b0}}), .in_24({32{1'b0}}), .in_25({32{1'b0}}),
    .in_26({32{1'b0}}), .in_27({32{1'b0}}), .in_28({32{1'b0}}), .in_29({32{1'b0}}), .in_30({32{1'b0}}),
    .in_31({32{1'b0}}), .out(O));
  BarrelShifter #(.Bits(32)) barrelshifter_1 (
    .in({multiplexer_1_out_2, multiplexer_1_out}), .shift(6'b001100), .out(barrelshifter_1_out));
  Add #(.Bits(32)) add_1 (.a(A), .b({multiplexer_1_out_2, multiplexer_1_out}), .c_i(1'b0), .s(add_1_s));  // open: c_o
  Sub #(.Bits(32)) sub_1 (.a(A), .b({multiplexer_1_out_2, multiplexer_1_out}), .c_i(1'b0), .s(sub_1_s));  // open: c_o
  Neg #(.Bits(32)) neg_1 (.in(A), .out(neg_1_out));
  assign and_1_out = A & {multiplexer_1_out_2, multiplexer_1_out};  // And and_1, 32 bits wide
  assign or_1_out = A | {multiplexer_1_out_2, multiplexer_1_out};  // Or or_1, 32 bits wide
  assign nand_1_out = ~(A & {multiplexer_1_out_2, multiplexer_1_out});  // NAnd nand_1, 32 bits wide
  assign xor_1_out = A ^ {multiplexer_1_out_2, multiplexer_1_out};  // XOr xor_1, 32 bits wide
  BarrelShifter #(.Bits(32)) barrelshifter_2 (.in(A), .shift(multiplexer_1_out), .out(barrelshifter_2_out));
  BarrelShifter #(.Bits(32), .direction("right")) barrelshifter_3 (
    .in(A), .shift(multiplexer_1_out), .out(barrelshifter_3_out));
  BarrelShifter #(.Bits(32), .barrelShifterMode("arithmetic"), .direction("right")) barrelshifter_4 (
    .in(A), .shift(multiplexer_1_out), .out(barrelshifter_4_out));
  BarrelShifter #(.Bits(32), .barrelShifterMode("rotate")) barrelshifter_5 (
    .in(A), .shift(multiplexer_1_out), .out(barrelshifter_5_out));
  BarrelShifter #(.Bits(32), .barrelShifterMode("rotate"), .direction("right")) barrelshifter_6 (
    .in(A), .shift(multiplexer_1_out), .out(barrelshifter_6_out));
endmodule
