// Digital circuit AddrSpaceDivider.dig as structural Verilog
module AddrSpaceDivider (
  input  [15:0] HighAddrSpace,
  input  [31:0] Addr,
  input  [31:0] IAddr,
  input  MemEnable,
  input  IEnable,
  output [15:0] AddrLow,
  output Sel,
  output [15:0] IAddrLow,
  output ISel,
  output [15:0] NextAddrSpace
);

  wire comparator_1_eq, comparator_2_eq;

  Comparator #(.Bits(16)) comparator_1 (.a(HighAddrSpace), .b(Addr[31:16]), .eq(comparator_1_eq));  // open: gt, lt
  Comparator #(.Bits(16)) comparator_2 (.a(IAddr[31:16]), .b(HighAddrSpace), .eq(comparator_2_eq));  // open: gt, lt
  and and_1 (Sel, MemEnable, comparator_1_eq);
  and and_2 (ISel, comparator_2_eq, IEnable);
  Add #(.Bits(16)) add_1 (.a(HighAddrSpace), .b(16'h1), .c_i(1'b0), .s(NextAddrSpace));  // open: c_o

  assign AddrLow = Addr[15:0];
  assign IAddrLow = IAddr[15:0];
endmodule
