// Digital circuit BranchUnit.dig as structural Verilog
module BranchUnit (
  input  Condition,
  input  [31:0] Source0,
  input  [31:0] Immediate,
  input  [31:0] RIP,
  input  BranchMode,
  input  BranchDestMode,
  input  BranchDelay,
  output LoadRIP,
  output [31:0] NewRIP,
  output WriteReg,
  output [31:0] RegValue
);

  wire [31:0] add_1_s, add_2_s, multiplexer_1_out;

  Multiplexer #(.Bits(32)) multiplexer_1 (.sel(BranchDelay), .in_0(32'h4), .in_1(32'hc), .out(multiplexer_1_out));
  or or_1 (LoadRIP, Condition, BranchMode);
  // Probe BranchMode on BranchMode
  Add #(.Bits(32)) add_1 (.a(Source0), .b(Immediate), .c_i(1'b0), .s(add_1_s));  // open: c_o
  Add #(.Bits(32)) add_2 (.a(Immediate), .b(RIP), .c_i(1'b0), .s(add_2_s));  // open: c_o
  Add #(.Bits(32)) add_3 (.a(RIP), .b(multiplexer_1_out), .c_i(1'b0), .s(RegValue));  // open: c_o
  Multiplexer #(.Bits(32)) multiplexer_2 (.sel(BranchDestMode), .in_0(add_1_s), .in_1(add_2_s), .out(NewRIP));

  assign WriteReg = BranchMode;
endmodule
