// Digital circuit Microcode.dig as structural Verilog
module Microcode (
  input  [5:0] Opcode,
  output [1:0] ALUOp,
  output ALUSwap,
  output ExecMode,
  output [1:0] MemMode,
  output ImmediateMode,
  output MemSize,
  output [1:0] Condition,
  output AddressMode,
  output BranchMode,
  output BranchDestModeMode
);

  LookUpTable #(.Bits(13)) lookuptable_1 (
    .in0(Opcode[0]), .in1(Opcode[1]), .in2(Opcode[2]), .in3(Opcode[3]), .in4(Opcode[4]), .in5(Opcode[5]),
    .out({BranchDestModeMode, BranchMode, AddressMode, Condition, MemSize, ImmediateMode, MemMode, ExecMode, ALUSwap, ALUOp}));

  // Notes on the sheet:
  //   contents of lookuptable_1 (hex, n*v repeats v):
  //   16*0,4*41,4b0,0,0,410,b0,0,0,808,4*45,43,42,1808,13*0,423,0,0
  //   ,23,0,0,1108,1208
endmodule
