// Digital circuit StageDecode.dig as structural Verilog
module StageDecode (
  input  [31:0] InstructionWord,
  input  Bubble,
  input  ForceBubble,
  input  ExecStall,
  input  [31:0] RIP,
  input  Clock,
  input  Reset,
  output [4:0] Dst,
  output [4:0] Src0,
  output [4:0] Src1,
  output [31:0] Immediate,
  output [31:0] RipOut,
  output BubbleOut,
  output [4:0] ALUOp,
  output ExecMode,
  output [1:0] MemMode,
  output ImmediateMode,
  output [1:0] MemSize,
  output [3:0] Condition,
  output AddressMode,
  output ALUSwap,
  output BranchMode,
  output BranchDestMode,
  output BranchDelay
);

  wire bubblereg_1_dataout, microcode_1_memsize, not_1_out;
  wire [1:0] microcode_1_aluop, microcode_1_condition;
  wire [2:0] IWord_q_3;
  wire [3:0] IWord_q_5;
  wire [5:0] IWord_q;
  wire [6:6] IWord_q_2;
  wire [11:5] IWord_q_4;
  wire [31:0] bitextender_1_out, bitextender_2_out, bitextender_3_out;

  not not_1 (not_1_out, ExecStall);
  Register #(.Bits(32)) IWord (
    .D(InstructionWord), .C(Clock), .en(not_1_out),
    .Q({IWord_q_4[11], IWord_q_5, IWord_q_4[6:5], IWord_q_3, Src1, Src0, Dst, IWord_q_2[6], IWord_q}));
  BubbleReg bubblereg_1 (
    .Data(Bubble), .Enable(not_1_out), .Clock(Clock), .Reset(Reset), .DataOut(bubblereg_1_dataout));
  Register #(.Bits(32)) u_RIP (.D(RIP), .C(Clock), .en(not_1_out), .Q(RipOut));
  or or_1 (BubbleOut, bubblereg_1_dataout, ForceBubble);
  Microcode microcode_1 (
    .Opcode(IWord_q), .ALUOp(microcode_1_aluop), .MemMode(MemMode), .Condition(microcode_1_condition),
    .ALUSwap(ALUSwap), .ExecMode(ExecMode), .ImmediateMode(ImmediateMode), .MemSize(microcode_1_memsize),
    .AddressMode(AddressMode), .BranchMode(BranchMode), .BranchDestModeMode(BranchDestMode),
    .BranchDelay(BranchDelay));
  BitExtender #(.inputBits(12), .outputBits(32)) bitextender_1 (
    .in({IWord_q_4[11], IWord_q_5, IWord_q_4[6:5], IWord_q_3, Src1[4:3]}), .out(bitextender_1_out));
  BitExtender #(.inputBits(20), .outputBits(32)) bitextender_2 (
    .in({IWord_q_4[11], IWord_q_5, IWord_q_4[6:5], IWord_q_3, Src1, Src0}), .out(bitextender_2_out));
  BitExtender #(.inputBits(12), .outputBits(32)) bitextender_3 (
    .in({IWord_q_4[11], IWord_q_5, IWord_q_4[6:5], Dst}), .out(bitextender_3_out));
  Multiplexer #(.Selector_Bits(2), .Bits(5)) multiplexer_1 (
    .sel(microcode_1_aluop), .in_0({IWord_q_4[6:5], IWord_q_3}), .in_1({IWord_q[1:0], Src1[2:0]}),
    .in_2(5'b00001), .in_3({5{1'b0}}), .out(ALUOp));
  Multiplexer #(.Selector_Bits(2), .Bits(32)) multiplexer_2 (
    .sel(IWord_q[5:4]), .in_0({32{1'b0}}), .in_1(bitextender_1_out), .in_2(bitextender_2_out),
    .in_3(bitextender_3_out), .out(Immediate));
  Multiplexer #(.Selector_Bits(2), .Bits(4)) multiplexer_3 (
    .sel(microcode_1_condition), .in_0(IWord_q_5), .in_1({1'b0, IWord_q_3}), .in_2({1'b1, IWord_q_3}),
    .in_3(4'b0000), .out(Condition));
  Multiplexer #(.Bits(2)) multiplexer_4 (
    .sel(microcode_1_memsize), .in_0(IWord_q_3[1:0]), .in_1(Src1[1:0]), .out(MemSize));
endmodule
