// Digital circuit StageExec.dig as structural Verilog
module StageExec (
  input  [4:0] MemBypassReg,
  input  [31:0] MemBypassValue,
  input  CanMemBypass,
  input  [4:0] WBypassReg,
  input  [31:0] WBypassValue,
  input  [4:0] FileBypassReg,
  input  [31:0] FileBypassValue,
  input  [4:0] Dst,
  input  [4:0] Src0,
  input  [31:0] Src0Data,
  input  [4:0] Src1,
  input  [31:0] Src1Data,
  input  [31:0] Immediate,
  input  [31:0] RIP,
  input  Bubble,
  input  [4:0] ALUOp,
  input  Mode,
  input  [1:0] MemMode,
  input  ImmediateMode,
  input  [1:0] MemSizeIn,
  input  [3:0] BranchOp,
  input  AddressMode,
  input  Clock,
  input  Reset,
  output [31:0] NewRIP,
  output LoadRIP,
  output [31:0] Value,
  output [4:0] DstOut,
  output [31:0] Address,
  output [1:0] MemModeOut,
  output BubbleOut,
  output Stall,
  output [1:0] MemSize
);

  wire AddressMode_t, and_1_out, branchunit_1_loadrip, branchunit_1_writereg, Bubble_t, ImMode, Mode_t,
       not_1_out;
  wire [3:0] BranchOp_t;
  wire [4:0] ALUOp_t, register_2_q, register_4_q;
  wire [31:0] alu_1_o, branchunit_1_regvalue, bypass_1_a, bypass_1_b, Immediate_t, register_3_q,
       register_5_q, RIP_t;

  not not_1 (not_1_out, Stall);
  Register #(.Bits(5)) register_1 (.D(Dst), .C(Clock), .en(not_1_out), .Q(DstOut));
  Register #(.Bits(5)) register_2 (.D(Src0), .C(Clock), .en(not_1_out), .Q(register_2_q));
  Register #(.Bits(32)) register_3 (.D(Src0Data), .C(Clock), .en(not_1_out), .Q(register_3_q));
  Register #(.Bits(5)) register_4 (.D(Src1), .C(Clock), .en(not_1_out), .Q(register_4_q));
  Register #(.Bits(32)) register_5 (.D(Src1Data), .C(Clock), .en(not_1_out), .Q(register_5_q));
  Register #(.Bits(32)) register_6 (.D(Immediate), .C(Clock), .en(not_1_out), .Q(Immediate_t));
  Register #(.Bits(32)) register_7 (.D(RIP), .C(Clock), .en(not_1_out), .Q(RIP_t));
  BubbleReg bubblereg_1 (.Data(Bubble), .Enable(not_1_out), .Clock(Clock), .Reset(Reset), .DataOut(Bubble_t));
  Register #(.Bits(5)) register_8 (.D(ALUOp), .C(Clock), .en(not_1_out), .Q(ALUOp_t));
  Register register_9 (.D(Mode), .C(Clock), .en(not_1_out), .Q(Mode_t));
  Register #(.Bits(2)) register_10 (.D(MemMode), .C(Clock), .en(not_1_out), .Q(MemModeOut));
  Register register_11 (.D(ImmediateMode), .C(Clock), .en(not_1_out), .Q(ImMode));
  Register #(.Bits(2)) register_12 (.D(MemSizeIn), .C(Clock), .en(not_1_out), .Q(MemSize));
  Register #(.Bits(4)) register_13 (.D(BranchOp), .C(Clock), .en(not_1_out), .Q(BranchOp_t));
  Register register_14 (.D(AddressMode), .C(Clock), .en(not_1_out), .Q(AddressMode_t));
  Bypass bypass_1 (
    .MemBypassReg(MemBypassReg), .MemBypassValue(MemBypassValue), .CanMemBypass(CanMemBypass),
    .WBypassReg(WBypassReg), .WBypassValue(WBypassValue), .FileBypassReg(FileBypassReg),
    .FileBypassValue(FileBypassValue), .Src0(register_2_q), .Src0Val(register_3_q), .Src1(register_4_q),
    .Src1Val(register_5_q), .A(bypass_1_a), .B(bypass_1_b), .Stall(Stall));
  and and_1 (and_1_out, Mode_t, ~branchunit_1_writereg);  // And
  or or_1 (BubbleOut, Stall, Bubble_t, and_1_out);
  ALU alu_1 (.A(bypass_1_a), .B(bypass_1_b), .Op(ALUOp_t), .Mode(ImMode), .Immediate(Immediate_t), .O(alu_1_o));
  BranchUnit branchunit_1 (
    .A(bypass_1_a), .B(bypass_1_b), .Immediate(Immediate_t), .RIP(RIP_t), .Op(BranchOp_t),
    .LoadRIP(branchunit_1_loadrip), .NewRIP(NewRIP), .RegValue(branchunit_1_regvalue),
    .WriteReg(branchunit_1_writereg));
  AddressUnit addressunit_1 (
    .Src0(bypass_1_a), .Immediate(Immediate_t), .RIP(RIP_t), .Mode(AddressMode_t), .Address(Address));
  Multiplexer #(.Bits(32)) multiplexer_1 (.sel(Mode_t), .in_0(alu_1_o), .in_1(branchunit_1_regvalue), .out(Value));
  and and_2 (LoadRIP, Mode_t, branchunit_1_loadrip, ~Bubble_t);  // And
endmodule
