// Digital circuit StageFetch.dig as structural Verilog
module StageFetch (
  input  BranchDelay,
  input  LoadRIP,
  input  [31:0] NewRIP,
  input  ExecStall,
  input  Clock,
  input  Reset,
  output StallDecode,
  output [31:0] Address,
  output Bubble
);

  wire fetchcontrol_1_pcchoice, fetchcontrol_1_storepc, fetchcontrol_1_zeropc;
  wire [31:0] add_1_s, multiplexer_1_out, multiplexer_2_out;

  FetchControl fetchcontrol_1 (
    .LoadRIP(LoadRIP), .ExecStall(ExecStall), .Reset(Reset), .BranchDelay(BranchDelay),
    .StallDecode(StallDecode), .Bubble(Bubble), .StorePC(fetchcontrol_1_storepc),
    .PCChoice(fetchcontrol_1_pcchoice), .ZeroPC(fetchcontrol_1_zeropc));
  Multiplexer #(.Bits(32)) multiplexer_1 (
    .sel(fetchcontrol_1_pcchoice), .in_0(add_1_s), .in_1(NewRIP), .out(multiplexer_1_out));
  Multiplexer #(.Bits(32)) multiplexer_2 (
    .sel(fetchcontrol_1_zeropc), .in_0(multiplexer_1_out), .in_1({32{1'b0}}), .out(multiplexer_2_out));
  Register #(.Bits(32), .isProgramCounter("true")) PC (
    .D(multiplexer_2_out), .C(Clock), .en(fetchcontrol_1_storepc), .Q(Address));
  Add #(.Bits(32)) add_1 (.a(32'h4), .b(Address), .c_i(1'b0), .s(add_1_s));  // open: c_o
endmodule
