// Digital circuit main.dig as structural Verilog
module main (
  input  Clock
);

  wire addrspacedivider_1_isel, addrspacedivider_1_read, addrspacedivider_1_write, addrspacedivider_2_isel,
       addrspacedivider_2_read, addrspacedivider_2_write, addrspacedivider_3_isel, addrspacedivider_3_read,
       addrspacedivider_3_write, addrspacedivider_4_isel, addrspacedivider_4_read, addrspacedivider_4_write,
       and_1_out, and_2_out, Clock_t, ClockMode_out, comparator_1_eq, MemEnable, MemWrite, PowOnReset_out,
       Pulse_out, Reset, Reset_out;
  wire [1:0] cpu_1_memsize;
  wire [13:0] addrspacedivider_1_addrlow, addrspacedivider_1_iaddrlow, addrspacedivider_2_addrlow,
       addrspacedivider_2_iaddrlow, addrspacedivider_3_addrlow, addrspacedivider_3_iaddrlow,
       addrspacedivider_4_addrlow, addrspacedivider_4_iaddrlow;
  wire [15:0] addrspacedivider_1_nextaddrspace, addrspacedivider_2_nextaddrspace,
       addrspacedivider_3_nextaddrspace;
  wire [29:0] Addr, IAddr;
  wire [31:0] cpu_1_address, cpu_1_dataout, cpu_1_iaddr, DataIn, IDataIn, MemDataIn, MemDataOut, MemIDataOut,
       ramdualaccess_1_d2, ramdualaccess_2_d2, ramdualaccess_3_d2, ramdualaccess_4_d2;

  DipSwitch ClockMode (.out(ClockMode_out));
  Button Pulse (.out(Pulse_out));
  Button u_Reset (.out(Reset_out));
  Reset #(.invertOutput("false")) PowOnReset (.out(PowOnReset_out));
  Multiplexer multiplexer_1 (.sel(ClockMode_out), .in_0(Pulse_out), .in_1(Clock), .out(Clock_t));
  or or_1 (Reset, Reset_out, PowOnReset_out);
  CPU cpu_1 (
    .DataIn(DataIn), .InstructionIn(IDataIn), .Enable(1'b1), .Clock(Clock_t), .Reset(Reset),
    .DataOut(cpu_1_dataout), .Address(cpu_1_address), .MemEnable(MemEnable), .MemWrite(MemWrite),
    .MemSize(cpu_1_memsize), .IAddr(cpu_1_iaddr));  // open: Stalls
  MemoryDriver memorydriver_1 (
    .CPUDataIn(cpu_1_dataout), .AddrIn(cpu_1_address), .MemDataIn(MemDataOut), .MemIDataIn(MemIDataOut),
    .Size(cpu_1_memsize), .IAddrIn(cpu_1_iaddr), .AddrOut(Addr), .IAddrOut(IAddr), .MemIDataOut(IDataIn),
    .WriteDataOut(MemDataIn), .ReadDataOut(DataIn));
  Comparator #(.Bits(30)) comparator_1 (.a(Addr), .b({30{1'b1}}), .eq(comparator_1_eq));  // open: gt, lt
  AddrSpaceDivider addrspacedivider_1 (
    .HighAddrSpace({16{1'b0}}), .Addr(Addr), .IAddr(IAddr), .MemEnable(MemEnable), .IEnable(1'b1),
    .WriteIn(MemWrite), .Write(addrspacedivider_1_write), .Read(addrspacedivider_1_read),
    .AddrLow(addrspacedivider_1_addrlow), .IAddrLow(addrspacedivider_1_iaddrlow),
    .ISel(addrspacedivider_1_isel), .NextAddrSpace(addrspacedivider_1_nextaddrspace));
  AddrSpaceDivider addrspacedivider_2 (
    .HighAddrSpace(addrspacedivider_1_nextaddrspace), .Addr(Addr), .IAddr(IAddr), .MemEnable(MemEnable),
    .IEnable(1'b1), .WriteIn(MemWrite), .Write(addrspacedivider_2_write), .Read(addrspacedivider_2_read),
    .AddrLow(addrspacedivider_2_addrlow), .IAddrLow(addrspacedivider_2_iaddrlow),
    .ISel(addrspacedivider_2_isel), .NextAddrSpace(addrspacedivider_2_nextaddrspace));
  AddrSpaceDivider addrspacedivider_3 (
    .HighAddrSpace(addrspacedivider_2_nextaddrspace), .Addr(Addr), .IAddr(IAddr), .MemEnable(MemEnable),
    .IEnable(1'b1), .WriteIn(MemWrite), .Write(addrspacedivider_3_write), .Read(addrspacedivider_3_read),
    .AddrLow(addrspacedivider_3_addrlow), .IAddrLow(addrspacedivider_3_iaddrlow),
    .ISel(addrspacedivider_3_isel), .NextAddrSpace(addrspacedivider_3_nextaddrspace));
  AddrSpaceDivider addrspacedivider_4 (
    .HighAddrSpace(addrspacedivider_3_nextaddrspace), .Addr(Addr), .IAddr(IAddr), .MemEnable(MemEnable),
    .IEnable(1'b1), .WriteIn(MemWrite), .Write(addrspacedivider_4_write), .Read(addrspacedivider_4_read),
    .AddrLow(addrspacedivider_4_addrlow), .IAddrLow(addrspacedivider_4_iaddrlow),
    .ISel(addrspacedivider_4_isel));  // open: NextAddrSpace
  and and_1 (and_1_out, MemWrite, MemEnable, comparator_1_eq);
  and and_2 (and_2_out, MemEnable, comparator_1_eq);
  assign MemDataOut = and_2_out ? {32{1'b0}} : 32'bz;  // Driver driver_1
  Terminal terminal_1 (.D(MemDataIn[6:0]), .C(Clock_t), .en(and_1_out));
  RAMDualAccess #(.AddrBits(14), .isProgramMemory("true"), .Bits(32)) ramdualaccess_1 (
    .str(addrspacedivider_1_write), .C(Clock_t), .ld(addrspacedivider_1_read),
    .A1(addrspacedivider_1_addrlow), .Din1(MemDataIn), .A2(addrspacedivider_1_iaddrlow), .D1(MemDataOut),
    .D2(ramdualaccess_1_d2));
  RAMDualAccess #(.AddrBits(14), .Bits(32)) ramdualaccess_2 (
    .str(addrspacedivider_2_write), .C(Clock_t), .ld(addrspacedivider_2_read),
    .A1(addrspacedivider_2_addrlow), .Din1(MemDataIn), .A2(addrspacedivider_2_iaddrlow), .D1(MemDataOut),
    .D2(ramdualaccess_2_d2));
  RAMDualAccess #(.AddrBits(14), .Bits(32)) ramdualaccess_3 (
    .str(addrspacedivider_3_write), .C(Clock_t), .ld(addrspacedivider_3_read),
    .A1(addrspacedivider_3_addrlow), .Din1(MemDataIn), .A2(addrspacedivider_3_iaddrlow), .D1(MemDataOut),
    .D2(ramdualaccess_3_d2));
  RAMDualAccess #(.AddrBits(14), .Bits(32)) ramdualaccess_4 (
    .str(addrspacedivider_4_write), .C(Clock_t), .ld(addrspacedivider_4_read),
    .A1(addrspacedivider_4_addrlow), .Din1(MemDataIn), .A2(addrspacedivider_4_iaddrlow), .D1(MemDataOut),
    .D2(ramdualaccess_4_d2));
  assign MemIDataOut = addrspacedivider_1_isel ? ramdualaccess_1_d2 : 32'bz;  // Driver driver_2
  assign MemIDataOut = addrspacedivider_2_isel ? ramdualaccess_2_d2 : 32'bz;  // Driver driver_3
  assign MemIDataOut = addrspacedivider_3_isel ? ramdualaccess_3_d2 : 32'bz;  // Driver driver_4
  assign MemIDataOut = addrspacedivider_4_isel ? ramdualaccess_4_d2 : 32'bz;  // Driver driver_5

  // Notes on the sheet:
  //   Clock: Hz: 500
endmodule
