// Logisim project risce.circ as structural Verilog
module CPU (
  input  Clock,
  input  Reset,
  input  [31:0] MemDataIn,
  output [31:0] MemAddress,
  output [31:0] MemDataOut,
  output MemEnable,
  output MemWrite,
  output [1:0] MemSize
);

  wire ExecStall, stagedecode_1_addressmode, stagedecode_1_bubbleout, stagedecode_1_execmode,
       stagedecode_1_immediatemode, stageexec_1_bubbleout, stageexec_1_loadrip, stagefetch_1_bubble,
       stagefetch_1_loadinstruction, stagefetch_1_loadsrip, stagememory_1_bubbleout, stagememory_1_canbypass,
       stagememory_1_memenable, stagememory_1_regwrite, stagewriteback_1_writedst;
  wire [1:0] stagedecode_1_memmode, stagedecode_1_memsize, stageexec_1_memmodeout, stageexec_1_memsize,
       stagememory_1_sizeout;
  wire [3:0] stagedecode_1_branchop;
  wire [4:0] stagedecode_1_aluop, stagedecode_1_dst, stagedecode_1_src0, stagedecode_1_src1,
       stageexec_1_dstout, stagememory_1_bypassreg, stagememory_1_dstout, stagewriteback_1_bypassreg,
       stagewriteback_1_dstout;
  wire [31:0] regfile_1_read0data, regfile_1_read1data, stagedecode_1_immediate, stagedecode_1_ripout,
       stageexec_1_address, stageexec_1_newrip, stageexec_1_value, stagefetch_1_address,
       stagememory_1_addressout, stagememory_1_bypassvalue, stagewriteback_1_bypassvalue,
       stagewriteback_1_dataout;

  StageFetch stagefetch_1 (
    .LoadRIP(stageexec_1_loadrip), .NewRIP(stageexec_1_newrip), .MemAccess(stagememory_1_memenable),
    .ExecStall(ExecStall), .Clock(Clock), .Reset(Reset), .LoadsRIP(stagefetch_1_loadsrip),
    .Address(stagefetch_1_address), .LoadInstruction(stagefetch_1_loadinstruction),
    .Bubble(stagefetch_1_bubble));
  Multiplexer #(.width(2)) multiplexer_1 (
    .in0(stagememory_1_sizeout), .in1(2'b10), .out(MemSize), .sel(stagefetch_1_loadinstruction));
  Multiplexer #(.width(32)) multiplexer_2 (
    .in0(stagememory_1_addressout), .in1(stagefetch_1_address), .out(MemAddress),
    .sel(stagefetch_1_loadinstruction));
  or or_1 (MemEnable, stagefetch_1_loadinstruction, stagememory_1_memenable);
  StageDecode stagedecode_1 (
    .InstructionWord(MemDataIn), .Bubble(stagefetch_1_bubble), .ForceBubble(stagefetch_1_loadsrip),
    .ExecStall(ExecStall), .RIP(stagefetch_1_address), .Clock(Clock), .Reset(Reset), .Dst(stagedecode_1_dst),
    .Src0(stagedecode_1_src0), .Src1(stagedecode_1_src1), .Immediate(stagedecode_1_immediate),
    .RIPOut(stagedecode_1_ripout), .BubbleOut(stagedecode_1_bubbleout), .ALUOp(stagedecode_1_aluop),
    .ExecMode(stagedecode_1_execmode), .MemMode(stagedecode_1_memmode),
    .ImmediateMode(stagedecode_1_immediatemode), .MemSize(stagedecode_1_memsize),
    .BranchOp(stagedecode_1_branchop), .AddressMode(stagedecode_1_addressmode));
  RegFile regfile_1 (
    .WriteReg(stagewriteback_1_dstout), .WriteEnable(stagewriteback_1_writedst),
    .Data(stagewriteback_1_dataout), .Read0Reg(stagedecode_1_src0), .Read1Reg(stagedecode_1_src1),
    .Clock(Clock), .Reset(Reset), .Read0Data(regfile_1_read0data), .Read1Data(regfile_1_read1data));
  StageExec stageexec_1 (
    .MemBypassReg(stagememory_1_bypassreg), .MemBypassValue(stagememory_1_bypassvalue),
    .CanMemBypass(stagememory_1_canbypass), .WBypassReg(stagewriteback_1_bypassreg),
    .WBypassValue(stagewriteback_1_bypassvalue), .Dst(stagedecode_1_dst), .Src0(stagedecode_1_src0),
    .Src0Val(regfile_1_read0data), .Src1(stagedecode_1_src1), .Src1Val(regfile_1_read1data),
    .Immediate(stagedecode_1_immediate), .RIP(stagedecode_1_ripout), .Bubble(stagedecode_1_bubbleout),
    .ALUOp(stagedecode_1_aluop), .Mode(stagedecode_1_execmode), .MemMode(stagedecode_1_memmode),
    .ImmediateMode(stagedecode_1_immediatemode), .MemSizeIn(stagedecode_1_memsize),
    .BranchOp(stagedecode_1_branchop), .AddressMode(stagedecode_1_addressmode), .Clock(Clock), .Reset(Reset),
    .NewRIP(stageexec_1_newrip), .LoadRIP(stageexec_1_loadrip), .Value(stageexec_1_value),
    .Address(stageexec_1_address), .DstOut(stageexec_1_dstout), .MemModeOut(stageexec_1_memmodeout),
    .BubbleOut(stageexec_1_bubbleout), .Stall(ExecStall), .MemSize(stageexec_1_memsize));
  StageMemory stagememory_1 (
    .Value(stageexec_1_value), .MemDataIn(MemDataIn), .Address(stageexec_1_address),
    .Mode(stageexec_1_memmodeout), .Dst(stageexec_1_dstout), .Bubble(stageexec_1_bubbleout),
    .Size(stageexec_1_memsize), .Clock(Clock), .Reset(Reset), .BypassValue(stagememory_1_bypassvalue),
    .BypassReg(stagememory_1_bypassreg), .CanBypass(stagememory_1_canbypass), .DataOut(MemDataOut),
    .AddressOut(stagememory_1_addressout), .MemEnable(stagememory_1_memenable), .MemWrite(MemWrite),
    .RegWrite(stagememory_1_regwrite), .DstOut(stagememory_1_dstout), .BubbleOut(stagememory_1_bubbleout),
    .SizeOut(stagememory_1_sizeout));
  StageWriteback stagewriteback_1 (
    .Data(MemDataOut), .Dst(stagememory_1_dstout), .WriteEnable(stagememory_1_regwrite),
    .Bubble(stagememory_1_bubbleout), .Clock(Clock), .Reset(Reset),
    .BypassValue(stagewriteback_1_bypassvalue), .BypassReg(stagewriteback_1_bypassreg),
    .DataOut(stagewriteback_1_dataout), .DstOut(stagewriteback_1_dstout), .WriteDst(stagewriteback_1_writedst));
endmodule

module RegFile (
  input  [4:0] WriteReg,
  input  WriteEnable,
  input  [31:0] Data,
  input  [4:0] Read0Reg,
  input  [4:0] Read1Reg,
  input  Clock,
  input  Reset,
  output [31:0] Read0Data,
  output [31:0] Read1Data
);

  wire Sel0, Sel1, Sel2, Sel3, Sel4, Sel5, Sel6, Sel7, Sel8, Sel9, Sel10, Sel11, Sel12, Sel13, Sel14, Sel15,
       Sel16, Sel17, Sel18, Sel19, Sel20, Sel21, Sel22, Sel23, Sel24, Sel25, Sel26, Sel27, Sel28, Sel29,
       Sel30, Sel31;
  wire [31:0] Reg1, Reg2, Reg3, Reg4, Reg5, Reg6, Reg7, Reg8, Reg9, Reg10, Reg11, Reg12, Reg13, Reg14, Reg15,
       Reg16, Reg17, Reg18, Reg19, Reg20, Reg21, Reg22, Reg23, Reg24, Reg25, Reg26, Reg27, Reg28, Reg29,
       Reg30, Reg31;

  Demultiplexer #(.select(5)) demultiplexer_1 (
    .out0(Sel0), .out1(Sel1), .out2(Sel2), .out3(Sel3), .out4(Sel4), .out5(Sel5), .out6(Sel6), .out7(Sel7),
    .out8(Sel8), .out9(Sel9), .out10(Sel10), .out11(Sel11), .out12(Sel12), .out13(Sel13), .out14(Sel14),
    .out15(Sel15), .out16(Sel16), .out17(Sel17), .out18(Sel18), .out19(Sel19), .out20(Sel20), .out21(Sel21),
    .out22(Sel22), .out23(Sel23), .out24(Sel24), .out25(Sel25), .out26(Sel26), .out27(Sel27), .out28(Sel28),
    .out29(Sel29), .out30(Sel30), .out31(Sel31), .in(WriteEnable), .sel(WriteReg));
  Register #(.width(32)) register_1 (.D(Data), .en(Sel1), .clk(Clock), .Q(Reg1), .clr(Reset));
  Register #(.width(32)) register_2 (.D(Data), .en(Sel2), .clk(Clock), .Q(Reg2), .clr(Reset));
  Register #(.width(32)) register_3 (.D(Data), .en(Sel3), .clk(Clock), .Q(Reg3), .clr(Reset));
  Register #(.width(32)) register_4 (.D(Data), .en(Sel4), .clk(Clock), .Q(Reg4), .clr(Reset));
  Register #(.width(32)) register_5 (.D(Data), .en(Sel5), .clk(Clock), .Q(Reg5), .clr(Reset));
  Register #(.width(32)) register_6 (.D(Data), .en(Sel6), .clk(Clock), .Q(Reg6), .clr(Reset));
  Register #(.width(32)) register_7 (.D(Data), .en(Sel7), .clk(Clock), .Q(Reg7), .clr(Reset));
  Register #(.width(32)) register_8 (.D(Data), .en(Sel8), .clk(Clock), .Q(Reg8), .clr(Reset));
  Register #(.width(32)) register_9 (.D(Data), .en(Sel9), .clk(Clock), .Q(Reg9), .clr(Reset));
  Register #(.width(32)) register_10 (.D(Data), .en(Sel10), .clk(Clock), .Q(Reg10), .clr(Reset));
  Register #(.width(32)) register_11 (.D(Data), .en(Sel11), .clk(Clock), .Q(Reg11), .clr(Reset));
  Register #(.width(32)) register_12 (.D(Data), .en(Sel12), .clk(Clock), .Q(Reg12), .clr(Reset));
  Register #(.width(32)) register_13 (.D(Data), .en(Sel13), .clk(Clock), .Q(Reg13), .clr(Reset));
  Register #(.width(32)) register_14 (.D(Data), .en(Sel14), .clk(Clock), .Q(Reg14), .clr(Reset));
  Register #(.width(32)) register_15 (.D(Data), .en(Sel15), .clk(Clock), .Q(Reg15), .clr(Reset));
  Register #(.width(32)) register_16 (.D(Data), .en(Sel16), .clk(Clock), .Q(Reg16), .clr(Reset));
  Register #(.width(32)) register_17 (.D(Data), .en(Sel17), .clk(Clock), .Q(Reg17), .clr(Reset));
  Register #(.width(32)) register_18 (.D(Data), .en(Sel18), .clk(Clock), .Q(Reg18), .clr(Reset));
  Register #(.width(32)) register_19 (.D(Data), .en(Sel19), .clk(Clock), .Q(Reg19), .clr(Reset));
  Register #(.width(32)) register_20 (.D(Data), .en(Sel20), .clk(Clock), .Q(Reg20), .clr(Reset));
  Register #(.width(32)) register_21 (.D(Data), .en(Sel21), .clk(Clock), .Q(Reg21), .clr(Reset));
  Register #(.width(32)) register_22 (.D(Data), .en(Sel22), .clk(Clock), .Q(Reg22), .clr(Reset));
  Register #(.width(32)) register_23 (.D(Data), .en(Sel23), .clk(Clock), .Q(Reg23), .clr(Reset));
  Register #(.width(32)) register_24 (.D(Data), .en(Sel24), .clk(Clock), .Q(Reg24), .clr(Reset));
  Register #(.width(32)) register_25 (.D(Data), .en(Sel25), .clk(Clock), .Q(Reg25), .clr(Reset));
  Register #(.width(32)) register_26 (.D(Data), .en(Sel26), .clk(Clock), .Q(Reg26), .clr(Reset));
  Register #(.width(32)) register_27 (.D(Data), .en(Sel27), .clk(Clock), .Q(Reg27), .clr(Reset));
  Register #(.width(32)) register_28 (.D(Data), .en(Sel28), .clk(Clock), .Q(Reg28), .clr(Reset));
  Register #(.width(32)) register_29 (.D(Data), .en(Sel29), .clk(Clock), .Q(Reg29), .clr(Reset));
  Register #(.width(32)) register_30 (.D(Data), .en(Sel30), .clk(Clock), .Q(Reg30), .clr(Reset));
  Register #(.width(32)) register_31 (.D(Data), .en(Sel31), .clk(Clock), .Q(Reg31), .clr(Reset));
  Multiplexer #(.select(5), .width(32)) multiplexer_1 (
    .in0({32{1'b0}}), .in1(Reg1), .in2(Reg2), .in3(Reg3), .in4(Reg4), .in5(Reg5), .in6(Reg6), .in7(Reg7),
    .in8(Reg8), .in9(Reg9), .in10(Reg10), .in11(Reg11), .in12(Reg12), .in13(Reg13), .in14(Reg14),
    .in15(Reg15), .in16(Reg16), .in17(Reg17), .in18(Reg18), .in19(Reg19), .in20(Reg20), .in21(Reg21),
    .in22(Reg22), .in23(Reg23), .in24(Reg24), .in25(Reg25), .in26(Reg26), .in27(Reg27), .in28(Reg28),
    .in29(Reg29), .in30(Reg30), .in31(Reg31), .out(Read0Data), .sel(Read0Reg));
  Multiplexer #(.select(5), .width(32)) multiplexer_2 (
    .in0({32{1'b0}}), .in1(Reg1), .in2(Reg2), .in3(Reg3), .in4(Reg4), .in5(Reg5), .in6(Reg6), .in7(Reg7),
    .in8(Reg8), .in9(Reg9), .in10(Reg10), .in11(Reg11), .in12(Reg12), .in13(Reg13), .in14(Reg14),
    .in15(Reg15), .in16(Reg16), .in17(Reg17), .in18(Reg18), .in19(Reg19), .in20(Reg20), .in21(Reg21),
    .in22(Reg22), .in23(Reg23), .in24(Reg24), .in25(Reg25), .in26(Reg26), .in27(Reg27), .in28(Reg28),
    .in29(Reg29), .in30(Reg30), .in31(Reg31), .out(Read1Data), .sel(Read1Reg));
endmodule

module StageFetch (
  input  LoadRIP,
  input  [31:0] NewRIP,
  input  MemAccess,
  input  ExecStall,
  input  Clock,
  input  Reset,
  output LoadsRIP,
  output [31:0] Address,
  output LoadInstruction,
  output Bubble
);

  wire and_1_out, and_2_out, not_1_out, or_1_out;
  wire [31:0] adder_1_out, multiplexer_1_out;

  not not_1 (not_1_out, ExecStall);
  and and_1 (and_1_out, ~MemAccess, not_1_out);  // AND_Gate
  and and_2 (and_2_out, LoadRIP, not_1_out);
  Multiplexer #(.width(32)) multiplexer_1 (.in0(adder_1_out), .in1(NewRIP), .out(multiplexer_1_out), .sel(LoadRIP));
  or or_1 (or_1_out, and_1_out, and_2_out);
  and and_3 (LoadsRIP, LoadRIP, or_1_out);
  Register #(.width(32)) RIP (.D(multiplexer_1_out), .en(or_1_out), .clk(Clock), .Q(Address), .clr(Reset));
  nor nor_1 (LoadInstruction, MemAccess, LoadRIP);
  or or_2 (Bubble, ~or_1_out, LoadRIP);  // OR_Gate
  Adder #(.width(32)) adder_1 (.a(32'h4), .b(Address), .out(adder_1_out), .cin(1'b0));  // open: cout
endmodule

module StageDecode (
  input  [31:0] InstructionWord,
  input  Bubble,
  input  ForceBubble,
  input  ExecStall,
  input  [31:0] RIP,
  input  Clock,
  input  Reset,
  output [4:0] Dst,
  output [4:0] Src0,
  output [4:0] Src1,
  output [31:0] Immediate,
  output [31:0] RIPOut,
  output BubbleOut,
  output [4:0] ALUOp,
  output ExecMode,
  output [1:0] MemMode,
  output ImmediateMode,
  output [1:0] MemSize,
  output [3:0] BranchOp,
  output AddressMode
);

  wire not_1_out, register_2_q;
  wire [1:0] bit_extender_5_out;
  wire [3:0] bit_extender_8_out, bit_extender_9_out, or_3_out;
  wire [4:0] bit_extender_6_out, multiplexer_2_out, or_2_out;
  wire [5:0] bit_extender_7_out;
  wire [6:0] Opcode;
  wire [9:0] pla_1_out;
  wire [31:0] bit_extender_2_out, bit_extender_3_out, bit_extender_4_out, register_1_q;

  not not_1 (not_1_out, ExecStall);
  Register #(.width(32)) register_1 (
    .D(InstructionWord), .en(not_1_out), .clk(Clock),
    .Q({register_1_q[31:22], Src1, Src0, Dst, register_1_q[6:0]}), .clr(Reset));
  Register #(.width(1)) register_2 (.D(Bubble), .en(not_1_out), .clk(Clock), .Q(register_2_q), .clr(Reset));
  or or_1 (BubbleOut, ForceBubble, register_2_q);
  Register #(.width(32)) register_3 (.D(RIP), .en(not_1_out), .clk(Clock), .Q(RIPOut), .clr(Reset));
  Bit_Extender #(.in_width(32), .out_width(7)) bit_extender_1 (
    .in({register_1_q[31:22], Src1, Src0, Dst, register_1_q[6:0]}), .out(Opcode));
  assign bit_extender_2_out = {{20{register_1_q[31]}}, {register_1_q[31:22], Src1[4:3]}};  // Bit_Extender bit_extender_2
  assign bit_extender_3_out = {{12{register_1_q[31]}}, {register_1_q[31:22], Src1, Src0}};  // Bit_Extender bit_extender_3
  assign bit_extender_4_out = {{20{register_1_q[31]}}, {register_1_q[31:25], Dst}};  // Bit_Extender bit_extender_4
  Bit_Extender #(.in_width(32), .out_width(2), .\type ("zero")) bit_extender_5 (
    .in({register_1_q[31:22], Src1, Src0, Dst, register_1_q[6:0]}), .out(bit_extender_5_out));
  Multiplexer #(.select(2), .width(32)) multiplexer_1 (
    .in0({32{1'b0}}), .in1(bit_extender_2_out), .in2(bit_extender_3_out), .in3(bit_extender_4_out),
    .out(Immediate), .sel(Opcode[5:4]));
  assign bit_extender_6_out = {{2{1'b0}}, Src1[2:0]};  // Bit_Extender bit_extender_6
  Multiplexer #(.select(2), .width(5)) multiplexer_2 (
    .in0({5{1'b0}}), .in1(5'b01000), .in2(5'b10000), .in3(5'b11000), .out(multiplexer_2_out),
    .sel(bit_extender_5_out));
  Bit_Extender #(.in_width(7), .out_width(6), .\type ("zero")) bit_extender_7 (.in(Opcode), .out(bit_extender_7_out));
  assign or_2_out = bit_extender_6_out | multiplexer_2_out;  // OR_Gate or_2, 5 bits wide
  PLA #(.in_width(6), .out_width(11), .\table ("000000 00000000000 # ALU A")) pla_1 (
    .in(bit_extender_7_out),
    .out({AddressMode, pla_1_out[9:8], MemSize, ImmediateMode, MemMode, ExecMode, pla_1_out[1:0]}));
  assign bit_extender_8_out = {{3{1'b0}}, register_1_q[22]};  // Bit_Extender bit_extender_8
  assign bit_extender_9_out = {{1{1'b0}}, register_1_q[24:22]};  // Bit_Extender bit_extender_9
  assign or_3_out = bit_extender_8_out | 4'b1000;  // OR_Gate or_3, 4 bits wide
  Multiplexer #(.select(2), .width(5)) multiplexer_3 (
    .in0(register_1_q[26:22]), .in1(or_2_out), .out(ALUOp), .sel(pla_1_out[1:0]));  // open: in2, in3
  Multiplexer #(.select(2), .width(4)) multiplexer_4 (
    .in0(bit_extender_9_out), .in1(or_3_out), .in2(4'b1010), .in3(4'b1011), .out(BranchOp),
    .sel(pla_1_out[9:8]));
endmodule

module StageExec (
  input  [4:0] MemBypassReg,
  input  [31:0] MemBypassValue,
  input  CanMemBypass,
  input  [4:0] WBypassReg,
  input  [31:0] WBypassValue,
  input  [4:0] Dst,
  input  [4:0] Src0,
  input  [31:0] Src0Val,
  input  [4:0] Src1,
  input  [31:0] Src1Val,
  input  [31:0] Immediate,
  input  [31:0] RIP,
  input  Bubble,
  input  [4:0] ALUOp,
  input  Mode,
  input  [1:0] MemMode,
  input  ImmediateMode,
  input  [1:0] MemSizeIn,
  input  [3:0] BranchOp,
  input  AddressMode,
  input  Clock,
  input  Reset,
  output [31:0] NewRIP,
  output LoadRIP,
  output [31:0] Value,
  output [31:0] Address,
  output [4:0] DstOut,
  output [1:0] MemModeOut,
  output BubbleOut,
  output Stall,
  output [1:0] MemSize
);

  wire AddressMode_t, and_1_out, branchunit_1_loadrip, branchunit_1_writereg, ImmediateMode_t, Mode_t,
       not_1_out, register_8_q;
  wire [3:0] BranchOp_t;
  wire [4:0] ALUOp_t, register_2_q, register_4_q;
  wire [31:0] A, alu_1_o, B, BranchValue, Immediate_t, register_3_q, register_5_q, RIP_t;

  not not_1 (not_1_out, Stall);
  Register #(.width(5)) register_1 (.D(Dst), .en(not_1_out), .clk(Clock), .Q(DstOut), .clr(Reset));
  Register #(.width(5)) register_2 (.D(Src0), .en(not_1_out), .clk(Clock), .Q(register_2_q), .clr(Reset));
  Register #(.width(32)) register_3 (.D(Src0Val), .en(not_1_out), .clk(Clock), .Q(register_3_q), .clr(Reset));
  Register #(.width(5)) register_4 (.D(Src1), .en(not_1_out), .clk(Clock), .Q(register_4_q), .clr(Reset));
  Register #(.width(32)) register_5 (.D(Src1Val), .en(not_1_out), .clk(Clock), .Q(register_5_q), .clr(Reset));
  Register #(.width(32)) register_6 (.D(Immediate), .en(not_1_out), .clk(Clock), .Q(Immediate_t), .clr(Reset));
  Register #(.width(32)) register_7 (.D(RIP), .en(not_1_out), .clk(Clock), .Q(RIP_t), .clr(Reset));
  Register #(.width(1)) register_8 (.D(Bubble), .en(not_1_out), .clk(Clock), .Q(register_8_q), .clr(Reset));
  Register #(.width(5)) register_9 (.D(ALUOp), .en(not_1_out), .clk(Clock), .Q(ALUOp_t), .clr(Reset));
  Register #(.width(1)) register_10 (.D(Mode), .en(not_1_out), .clk(Clock), .Q(Mode_t), .clr(Reset));
  Register #(.width(2)) register_11 (.D(MemMode), .en(not_1_out), .clk(Clock), .Q(MemModeOut), .clr(Reset));
  Register #(.width(1)) register_12 (.D(ImmediateMode), .en(not_1_out), .clk(Clock), .Q(ImmediateMode_t), .clr(Reset));
  Register #(.width(2)) register_13 (.D(MemSizeIn), .en(not_1_out), .clk(Clock), .Q(MemSize), .clr(Reset));
  Register #(.width(4)) register_14 (.D(BranchOp), .en(not_1_out), .clk(Clock), .Q(BranchOp_t), .clr(Reset));
  Register #(.width(1)) register_15 (.D(AddressMode), .en(not_1_out), .clk(Clock), .Q(AddressMode_t), .clr(Reset));
  and and_1 (and_1_out, Mode_t, ~branchunit_1_writereg);  // AND_Gate
  or or_1 (BubbleOut, register_8_q, and_1_out, Stall);
  RegBypass regbypass_1 (
    .MemBypassReg(MemBypassReg), .MemBypassValue(MemBypassValue), .CanMemBypass(CanMemBypass),
    .WBypassReg(WBypassReg), .WBypassValue(WBypassValue), .Src0(register_2_q), .Src0Val(register_3_q),
    .Src1(register_4_q), .Src1Val(register_5_q), .Stall(Stall), .Src0ValOut(A), .Src1ValOut(B));
  ALU alu_1 (.A(A), .B(B), .Immediate(Immediate_t), .ImmediateMode(ImmediateMode_t), .Op(ALUOp_t), .O(alu_1_o));
  AddressUnit addressunit_1 (.Src0(A), .Immediate(Immediate_t), .RIP(RIP_t), .Mode(AddressMode_t), .Address(Address));
  BranchUnit branchunit_1 (
    .A(A), .B(B), .Immediate(Immediate_t), .RIP(RIP_t), .Op(BranchOp_t), .LoadRIP(branchunit_1_loadrip),
    .NewRIP(NewRIP), .RegValue(BranchValue), .WriteReg(branchunit_1_writereg));
  and and_2 (LoadRIP, Mode_t, branchunit_1_loadrip);
  Multiplexer #(.width(32)) multiplexer_1 (.in0(alu_1_o), .in1(BranchValue), .out(Value), .sel(Mode_t));

  // Other names for the same wires on the sheet: MemMode_t[1:0] = MemModeOut
endmodule

module StageMemory (
  input  [31:0] Value,
  input  [31:0] MemDataIn,
  input  [31:0] Address,
  input  [1:0] Mode,
  input  [4:0] Dst,
  input  Bubble,
  input  [1:0] Size,
  input  Clock,
  input  Reset,
  output [31:0] BypassValue,
  output [4:0] BypassReg,
  output CanBypass,
  output [31:0] DataOut,
  output [31:0] AddressOut,
  output MemEnable,
  output MemWrite,
  output RegWrite,
  output [4:0] DstOut,
  output BubbleOut,
  output [1:0] SizeOut
);

  wire and_1_out, decoder_1_out0, decoder_1_out1, decoder_1_out3, not_1_out, not_2_out;
  wire [1:0] register_3_q;

  Register #(.width(32)) register_1 (.D(Value), .clk(Clock), .Q(BypassValue), .clr(Reset));  // open: en
  Register #(.width(32)) register_2 (.D(Address), .clk(Clock), .Q(AddressOut), .clr(Reset));  // open: en
  Register #(.width(2)) register_3 (.D(Mode), .clk(Clock), .Q(register_3_q), .clr(Reset));  // open: en
  Register #(.width(5)) register_4 (.D(Dst), .clk(Clock), .Q(DstOut), .clr(Reset));  // open: en
  Register #(.width(1)) register_5 (.D(Bubble), .clk(Clock), .Q(BubbleOut), .clr(Reset));  // open: en
  Register #(.width(2)) register_6 (.D(Size), .Q(SizeOut));  // open: en, clk, clr
  Decoder #(.select(2)) decoder_1 (
    .out0(decoder_1_out0), .out1(decoder_1_out1), .out2(MemWrite), .out3(decoder_1_out3), .sel(register_3_q),
    .en(not_1_out));
  not not_1 (not_1_out, BubbleOut);
  or or_1 (MemEnable, decoder_1_out3, MemWrite);
  Multiplexer #(.select(2), .width(32)) multiplexer_1 (
    .in0(BypassValue), .in1(AddressOut), .in2({32{1'b0}}), .in3(MemDataIn), .out(DataOut), .sel(register_3_q));
  or or_2 (RegWrite, decoder_1_out0, decoder_1_out1, decoder_1_out3);
  Multiplexer #(.width(5)) multiplexer_2 (.in0(DstOut), .in1({5{1'b0}}), .out(BypassReg), .sel(not_2_out));
  not not_2 (not_2_out, and_1_out);
  not not_3 (CanBypass, MemWrite);
  and and_1 (and_1_out, RegWrite, not_1_out);
endmodule

module StageWriteback (
  input  [31:0] Data,
  input  [4:0] Dst,
  input  WriteEnable,
  input  Bubble,
  input  Clock,
  input  Reset,
  output [31:0] BypassValue,
  output [4:0] BypassReg,
  output [31:0] DataOut,
  output [4:0] DstOut,
  output WriteDst
);

  wire or_1_out, register_3_q, register_4_q;

  Register #(.width(32)) register_1 (.D(Data), .clk(Clock), .Q(BypassValue), .clr(Reset));  // open: en
  Register #(.width(5)) register_2 (.D(Dst), .clk(Clock), .Q(DstOut), .clr(Reset));  // open: en
  Register #(.width(1)) register_3 (.D(WriteEnable), .clk(Clock), .Q(register_3_q), .clr(Reset));  // open: en
  Register #(.width(1)) register_4 (.D(Bubble), .clk(Clock), .Q(register_4_q), .clr(Reset));  // open: en
  or or_1 (or_1_out, ~register_3_q, register_4_q);  // OR_Gate
  and and_1 (WriteDst, register_3_q, ~register_4_q);  // AND_Gate
  Multiplexer #(.width(5)) multiplexer_1 (.in0(DstOut), .in1({5{1'b0}}), .out(BypassReg), .sel(or_1_out));

  assign DataOut = BypassValue;
endmodule

module RegBypass (
  input  [4:0] MemBypassReg,
  input  [31:0] MemBypassValue,
  input  CanMemBypass,
  input  [4:0] WBypassReg,
  input  [31:0] WBypassValue,
  input  [4:0] Src0,
  input  [31:0] Src0Val,
  input  [4:0] Src1,
  input  [31:0] Src1Val,
  output Stall,
  output [31:0] Src0ValOut,
  output [31:0] Src1ValOut
);

  wire singleregbypass_1_stall, singleregbypass_2_stall;

  SingleRegBypass singleregbypass_1 (
    .MemBypassReg(MemBypassReg), .MemBypassValue(MemBypassValue), .CanMemBypass(CanMemBypass),
    .WBypassReg(WBypassReg), .WBypassValue(WBypassValue), .RegName(Src0), .RegValue(Src0Val),
    .Stall(singleregbypass_1_stall), .Value(Src0ValOut));
  SingleRegBypass singleregbypass_2 (
    .MemBypassReg(MemBypassReg), .MemBypassValue(MemBypassValue), .CanMemBypass(CanMemBypass),
    .WBypassReg(WBypassReg), .WBypassValue(WBypassValue), .RegName(Src1), .RegValue(Src1Val),
    .Stall(singleregbypass_2_stall), .Value(Src1ValOut));
  or or_1 (Stall, singleregbypass_1_stall, singleregbypass_2_stall);
endmodule

module SingleRegBypass (
  input  [4:0] MemBypassReg,
  input  [31:0] MemBypassValue,
  input  CanMemBypass,
  input  [4:0] WBypassReg,
  input  [31:0] WBypassValue,
  input  [4:0] RegName,
  input  [31:0] RegValue,
  output Stall,
  output [31:0] Value
);

  wire bypasstester_1_shouldbypass, bypasstester_2_shouldbypass;
  wire [31:0] multiplexer_2_out;

  and and_1 (Stall, bypasstester_1_shouldbypass, ~CanMemBypass);  // AND_Gate
  BypassTester bypasstester_1 (.BypassReg(MemBypassReg), .SrcReg(RegName), .ShouldBypass(bypasstester_1_shouldbypass));
  BypassTester bypasstester_2 (.BypassReg(WBypassReg), .SrcReg(RegName), .ShouldBypass(bypasstester_2_shouldbypass));
  Multiplexer #(.width(32)) multiplexer_1 (
    .in0(multiplexer_2_out), .in1(MemBypassValue), .out(Value), .sel(bypasstester_1_shouldbypass));
  Multiplexer #(.width(32)) multiplexer_2 (
    .in0(RegValue), .in1(WBypassValue), .out(multiplexer_2_out), .sel(bypasstester_2_shouldbypass));
endmodule

module BypassTester (
  input  [4:0] BypassReg,
  input  [4:0] SrcReg,
  output ShouldBypass
);

  wire comparator_1_eq, or_1_out;

  Comparator #(.mode("unsigned"), .width(5)) comparator_1 (
    .a(BypassReg), .b(SrcReg), .eq(comparator_1_eq));  // open: gt, lt
  or or_1 (or_1_out, BypassReg[0], BypassReg[1], BypassReg[2], BypassReg[3], BypassReg[4]);
  and and_1 (ShouldBypass, or_1_out, comparator_1_eq);
endmodule

module BranchUnit (
  input  [31:0] A,
  input  [31:0] B,
  input  [31:0] Immediate,
  input  [31:0] RIP,
  input  [3:0] Op,
  output LoadRIP,
  output [31:0] NewRIP,
  output [31:0] RegValue,
  output WriteReg
);

  wire comparator_1_gt, comparator_1_lt, comparator_2_eq, comparator_2_gt, comparator_2_lt, comparator_3_eq,
       comparator_4_eq, not_1_out, not_2_out, not_3_out, not_4_out, not_5_out;
  wire [31:0] adder_2_out;

  Adder #(.width(32)) adder_1 (.a(Immediate), .b(RIP), .out(RegValue));  // open: cin, cout
  Comparator #(.width(32)) comparator_1 (.a(A), .b(B), .gt(comparator_1_gt), .lt(comparator_1_lt));  // open: eq
  Comparator #(.mode("unsigned"), .width(32)) comparator_2 (
    .a(A), .b(B), .gt(comparator_2_gt), .eq(comparator_2_eq), .lt(comparator_2_lt));
  Adder #(.width(32)) adder_2 (.a(A), .b(RegValue), .out(adder_2_out));  // open: cin, cout
  Comparator #(.mode("unsigned"), .width(4)) comparator_3 (.a(4'b1010), .b(Op), .eq(comparator_3_eq));  // open: gt, lt
  Comparator #(.mode("unsigned"), .width(4)) comparator_4 (.a(Op), .b(4'b1011), .eq(comparator_4_eq));  // open: gt, lt
  Multiplexer #(.width(32)) multiplexer_1 (.in0(RegValue), .in1(adder_2_out), .out(NewRIP), .sel(comparator_3_eq));
  or or_1 (WriteReg, comparator_3_eq, comparator_4_eq);
  not not_1 (not_1_out, comparator_1_gt);
  not not_2 (not_2_out, comparator_1_lt);
  not not_3 (not_3_out, comparator_2_gt);
  not not_4 (not_4_out, comparator_2_lt);
  Multiplexer #(.select(4)) multiplexer_2 (
    .in0(comparator_1_gt), .in1(comparator_1_lt), .in2(comparator_2_gt), .in3(comparator_2_lt),
    .in4(not_1_out), .in5(not_2_out), .in6(not_3_out), .in7(not_4_out), .in8(comparator_2_eq),
    .in9(not_5_out), .in10(1'b1), .in11(1'b1), .in12(1'b1), .in13(1'b1), .in14(1'b1), .in15(1'b1),
    .out(LoadRIP), .sel(Op));
  not not_5 (not_5_out, comparator_2_eq);
endmodule

module ALU (
  input  [31:0] A,
  input  [31:0] B,
  input  [31:0] Immediate,
  input  ImmediateMode,
  input  [4:0] Op,
  output [31:0] O
);

  wire [31:0] multiplexer_1_out;

  Multiplexer #(.width(32)) multiplexer_1 (.in0(B), .in1(Immediate), .out(multiplexer_1_out), .sel(ImmediateMode));
endmodule

module AddressUnit (
  input  [31:0] Src0,
  input  [31:0] Immediate,
  input  [31:0] RIP,
  input  Mode,
  output [31:0] Address
);

  wire [31:0] adder_1_out, adder_2_out;

  Adder #(.width(32)) adder_1 (.a(Src0), .b(Immediate), .out(adder_1_out));  // open: cin, cout
  Adder #(.width(32)) adder_2 (.a(adder_1_out), .b(RIP), .out(adder_2_out));  // open: cin, cout
  Multiplexer #(.width(32)) multiplexer_1 (.in0(adder_1_out), .in1(adder_2_out), .out(Address), .sel(Mode));
endmodule
